# Fritzing sketch UNO_UIPEthernet_Mqtt (saved by Fritzing 0.9.3b)
circuit board: 10.3312cm x 6.74352cm
breadboards: 1

parts:
  元件1 = ENC28J60 Breakout Board
  DHT11_1 = DHT11 module
  LED1 = LED - 5mm [color="Yellow (585nm)" package="5 mm [THT]"]
  LED2 = LED - 5mm [color="Red (633nm)" package="5 mm [THT]"]
  LED3 = LED - 5mm [color="Blue (430nm)" package="5 mm [THT]"]
  R1 = Resistor [tolerance=±5% resistance=220 package=THT]
  R2 = Resistor [tolerance=±5% resistance=220 package=THT]
  R3 = Resistor [tolerance=±5% resistance=220 package=THT]
  R4 = Resistor [tolerance=±5% resistance=220 package=THT]
  LED5 = LED - 5mm [color="Green (565nm)" package="5 mm [THT]"]
  元件2 = Arduino Uno (Rev3)

nets:
  VCC: 元件1.VCC, DHT11_1.VCC, 元件2.5V
  GND: 元件1.GND, DHT11_1.GND, LED1.cathode, LED2.cathode, LED3.cathode, R1.Pin_0, R1.Pin_1, R2.Pin_0, R2.Pin_1, R3.Pin_0, R3.Pin_1, R4.Pin_0, R4.Pin_1, LED5.cathode, 元件2.GND
  N1: 元件1.CS, 元件2.D10_PWM/SS
  N2: 元件1.SI, 元件2.D11_PWM/MOSI
  N3: 元件1.SCK, 元件2.D13/SCK
  N4: 元件1.SO, 元件2.D12/MISO
  N5: DHT11_1.DATA, 元件2.D8
  N6: LED1.anode, 元件2.D5_PWM
  N7: LED2.anode, 元件2.D4
  N8: LED3.anode, 元件2.D3_PWM
  N9: LED5.anode, 元件2.D6_PWM

custom parts:
  ENC28J60 Breakout Board: This is a breakout board for the Microchip ENC28J60 stand-alone ethernet controller. The ENC28J60 has an SPI interface. It operates at 3.3 Volts.
  DHT11 module: DHT11 black pcb module

// code stored in the sketch: UNO_UIPEthernet_Mqtt.ino
// UIPEthernet.h  https://github.com/UIPEthernet/UIPEthernet
// PubSubClient.h  https://github.com/knolleary/pubsubclient
//??RAM https://andrologiciels.wordpress.com/arduino/electronique/ram/

//#include <avr/pgmspace.h>

//#include <Wire.h>
//#include <LiquidCrystal_I2C.h>
//LiquidCrystal_I2C lcd(0x27, 20, 4);

#include <UIPEthernet.h>
#include <PubSubClient.h>
#define STATIC 0 // ??? 1 ??? DHCP

// Update these with values suitable for your network.
uint8_t mac[6] = {0x00, 0xAA, 0xBB, 0xCC, 0xDE, 0x02};
IPAddress ip(192, 168, 0, 125);
//IPAddress dnss(192, 168, 0, 1);// the dns server ip
//IPAddress gateway(192, 168, 0, 1);// the router's gateway address:
//IPAddress subnet(255, 255, 255, 0);// the subnet:


//const char* mqtt_server = "MQTTGO.io";
const char* mqtt_server = "broker.emqx.io";
const char* mqttUserName = "QWEQWE";  // ??????Username?
const char* mqttPwd = "QWEQWE";  //  ??????Password
const char* topicToSub = "inTopic88888"; //??in
const char* topicToPub = "outTopic88888"; //??out


const PROGMEM char msg[22];


EthernetClient ethClient;
PubSubClient client(ethClient);

unsigned long  previous_millis_A = 0; //??????millis
unsigned long  interval_A = 10 * 1000; //??5???


#include "DHT.h"
#define DHTPIN 8      //??DHT11 Data
#define DHTTYPE DHT11 //??DHT11
DHT dht(DHTPIN, DHTTYPE); // Initialize DHT sensor
float h, t;

int led1 = 3;
int led2 = 4;
int led3 = 5;
int led4 = 6;




// Callback function
void callback(char* topic, byte* message, unsigned int length) {
  String receivedMsg;
  for (unsigned int i = 0; i < length; i++) {
    receivedMsg += (char)message[i];
  }
  //  Serial.print(F("??????? "));
  //  Serial.print(topic);
  //  Serial.print(F(",Message: "));
  //  Serial.println(receivedMsg);
  if (String(topic) == topicToSub) {

    if (receivedMsg == ("led1on")) {
      //      Serial.println(F("led1on"));
      digitalWrite(led1, HIGH);
    } else if (receivedMsg == "led1off") {
      //      Serial.println(F("led1off"));
      digitalWrite(led1, LOW);
    }

    if (receivedMsg == ("led2on")) {
      //      Serial.println(F("led2on"));
      digitalWrite(led2, HIGH);
    } else if (receivedMsg == "led2off") {
      //      Serial.println(F("led2off"));
      digitalWrite(led2, LOW);
    }


    if (receivedMsg == ("led3on")) {
      //      Serial.println(F("led3on"));
      digitalWrite(led3, HIGH);
    } else if (receivedMsg == "led3off") {
      //      Serial.println(F("led3off"));
      digitalWrite(led3, LOW);
    }

    if (receivedMsg == ("led4on")) {
      //      Serial.println(F("led3on"));
      digitalWrite(led4, HIGH);
    } else if (receivedMsg == "led4off") {
      //      Serial.println(F("led3off"));
      digitalWrite(led4, LOW);
    }

    //-------------------------------------------------
  }
}


void reconnect() {
  // Loop until we're reconnected
  while (!client.connected()) {
    Serial.print(F("???? MQTT ??..."));
    // Create a random client ID
    String clientId = "UNO_Client-";
    clientId += String(random(0xffff), HEX);
    // Attempt to connect
    if (client.connect(clientId.c_str(), mqttUserName, mqttPwd)) {
      //    if (client.connect(clientId.c_str())) {
      Serial.print(F("??"));Serial.println(client.state());
      // Once connected, publish an announcement...
      client.publish(topicToPub, "hello world");
      // ... and resubscribe
      client.subscribe(topicToSub);
    } else {
      Serial.print(F("failed, rc="));
      Serial.print(client.state());
      Serial.println(F(" 5 ????"));
      // Wait 5 seconds before retrying
      delay(5000);
    }
  }
}

void setup()
{

  Serial.begin(9600);



#if STATIC
  Ethernet.begin(mac, ip);
  //    Ethernet.begin(mac, ip, dnss, gateway, subnet);
#else
  if (Ethernet.begin(mac) == 0) {
    //    Serial.println(F("Failed to configure Ethernet using DHCP"));
  }
#endif

  //  Serial.print(F("localIP: "));
  //  Serial.println(Ethernet.localIP());
  //  Serial.print(F("subnetMask: "));
  //  Serial.println(Ethernet.subnetMask());
  //  Serial.print(F("gatewayIP: "));
  //  Serial.println(Ethernet.gatewayIP());
  //  Serial.print(F("dnsServerIP: "));
  //  Serial.println(Ethernet.dnsServerIP());

  //---------mqtt------------
  client.setServer(mqtt_server, 1883);
  client.setCallback(callback);

  //------lcd--------
  //    lcd.init(); // initialize LCD
  //    lcd.backlight(); // ????
  //    lcd.setCursor(0, 0);
  //    lcd.print(F("IP:"));
  //    lcd.print(Ethernet.localIP());
  //  lcd.setCursor(0, 1);
  //  lcd.print(F("Mask:"));
  //  lcd.print(Ethernet.subnetMask());
  //  lcd.setCursor(0, 2);
  //  lcd.print(F("gw:"));
  //  lcd.print(Ethernet.gatewayIP());
  //  lcd.setCursor(0, 3);
  //  lcd.print(F("dns:"));
  //  lcd.print(Ethernet.dnsServerIP());



  //  delay(1500);

  //  lcd.setCursor(0, 1);
  //  lcd.print(F("                    "));
  //  lcd.setCursor(0, 3);
  //  lcd.print(F("                    "));
  //
  //  lcd.setCursor(0, 3);
  //  lcd.print(F("LED1:N"));
  //
  //  lcd.setCursor(7, 3);
  //  lcd.print(F("LED2:N"));
  //
  //  lcd.setCursor(14, 3);
  //  lcd.print(F("LED3:N"));


  pinMode(led1, OUTPUT);
  pinMode(led2, OUTPUT);
  pinMode(led3, OUTPUT);
  pinMode(led4, OUTPUT);



  dht.begin();//??DHT

}

void loop()
{

  h = dht.readHumidity();//????
  t = dht.readTemperature();//??????
  //  float f = dht.readTemperature(true);//??????

  if (!client.connected()) {
    reconnect();
  }

  client.loop();


  // ??????????? --------------------
  // ?? 1 -- ???????
  // ?? 5 ?????

  unsigned long int current_millis_A = millis();              //current_millis_A = 2000
  if ((current_millis_A - previous_millis_A) >= interval_A) { //(2000 - 1000) >= 1000
    previous_millis_A = current_millis_A;

    String msgStr =  "{\"T\":" +  String(t) + ",\"H\":" + String(h) + "}"; // ??MQTT???JSON??????
    msgStr.toCharArray(msg, 22); // ?String??????????? ????????212????65536?????



    client.publish(topicToPub, msg); // ??MQTT?????????????212????65536?????

    //        Serial.print(F("Publish message: "));
    Serial.println(msg);

//    Serial.print(F("SRAM:"));
//    Serial.println( freeRam());
    msgStr = "";
  }

  //-----------------------------------------------


}


//int freeRam ()
//{
//  extern int __heap_start, *__brkval;
//  int v;
//  return (int) &v - (__brkval == 0 ? (int) &__heap_start : (int) __brkval);
//}
